// Logisim project cpu.circ as structural Verilog: 1 circuit, main circuit main
module main (
  input  CLK_RUN,
  input  CLK_HLT,
  input  [7:0] in_3,
  input  [15:0] in_4,
  input  in_5,
  input  in_6,
  input  IP_HI_TO_DATA,
  input  IP_LO_TO_DATA,
  input  A_TO_DATA,
  input  DATA_TO_A,
  input  DATA_TO_IP_HI,
  input  DATA_TO_IP_LO,
  input  IP_TO_ADDR,
  input  A_TO_X,
  input  IP_INC,
  input  ADDR_TO_IP,
  input  DATA_TO_MAR_HI,
  input  DATA_TO_MAR_LO,
  input  MAR_INC,
  input  ADDR_TO_MAR,
  input  DATA_TO_Y,
  input  MDR_TO_DATA,
  input  DATA_TO_MDR,
  input  B_TO_DATA,
  input  DATA_TO_B,
  input  C_TO_DATA,
  input  DATA_TO_C,
  input  D_TO_DATA,
  input  DATA_TO_D,
  input  in_30,
  output [7:0] out_31,
  output [15:0] out_32,
  output [15:0] out_33,
  output [7:0] out_34,
  output [7:0] out_35,
  output [15:0] out_36,
  output [7:0] out_37,
  output [7:0] out_38,
  output [7:0] out_39,
  output [7:0] out_40,
  output [7:0] out_41
);

  wire and_1_out, and_2_out, CLK, CLK_STEP_out, clock_1_out, minus_CLK, nor_1_out, nor_2_out, nor_3_out,
       nor_4_out, not_1_out, not_2_out, not_3_out, or_1_out, or_2_out, or_3_out, RST;
  wire [7:0] controlled_buffer_7_out, controlled_buffer_12_out;
  wire [15:0] controlled_buffer_8_out;

  Register register_1 (.D(out_31), .en(DATA_TO_A), .Q(out_34), .clk(CLK));  // open: clr
  assign out_31 = A_TO_DATA ? out_34 : 8'bz;  // Controlled_Buffer controlled_buffer_1
  Register register_2 (.D(out_34), .en(A_TO_X), .Q(out_35), .clk(CLK));  // open: clr
  Register register_3 (.D(out_31), .en(DATA_TO_Y), .Q(out_37), .clk(CLK));  // open: clr
  assign out_31 = B_TO_DATA ? out_39 : 8'bz;  // Controlled_Buffer controlled_buffer_2
  Register register_4 (.D(out_31), .en(DATA_TO_B), .Q(out_39), .clk(CLK));  // open: clr
  Register register_5 (.D(out_31), .en(DATA_TO_C), .Q(out_40), .clk(CLK));  // open: clr
  assign out_31 = C_TO_DATA ? out_40 : 8'bz;  // Controlled_Buffer controlled_buffer_3
  Register register_6 (.D(out_31), .en(DATA_TO_D), .Q(out_41), .clk(CLK));  // open: clr
  assign out_31 = D_TO_DATA ? out_41 : 8'bz;  // Controlled_Buffer controlled_buffer_4
  Button CLK_STEP (.out(CLK_STEP_out));
  Button u_RST (.out(RST));
  Clock clock_1 (.out(clock_1_out));
  and and_1 (and_1_out, clock_1_out, CLK_RUN);
  not not_1 (not_1_out, CLK_RUN);
  and and_2 (and_2_out, not_1_out, CLK_STEP_out);
  not not_2 (not_2_out, CLK_HLT);
  assign out_31 = in_5 ? in_3 : 8'bz;  // Controlled_Buffer controlled_buffer_5
  assign out_31 = IP_LO_TO_DATA ? out_33[7:0] : 8'bz;  // Controlled_Buffer controlled_buffer_6
  assign controlled_buffer_7_out = DATA_TO_IP_LO ? out_31 : 8'bz;  // Controlled_Buffer controlled_buffer_7
  assign controlled_buffer_8_out[7:0] = DATA_TO_MAR_LO ? out_31 : 8'bz;  // Controlled_Buffer controlled_buffer_8
  assign out_38 = DATA_TO_MDR ? out_31 : 8'bz;  // Controlled_Buffer controlled_buffer_9
  assign out_31 = MDR_TO_DATA ? out_38 : 8'bz;  // Controlled_Buffer controlled_buffer_10
  or or_1 (or_1_out, and_1_out, and_2_out);
  nor nor_1 (nor_1_out, DATA_TO_IP_LO, ADDR_TO_IP);
  assign controlled_buffer_7_out = nor_1_out ? out_33[7:0] : 8'bz;  // Controlled_Buffer controlled_buffer_11
  assign controlled_buffer_12_out = DATA_TO_IP_HI ? out_31 : 8'bz;  // Controlled_Buffer controlled_buffer_12
  nor nor_2 (nor_2_out, DATA_TO_MAR_LO, ADDR_TO_MAR);
  assign controlled_buffer_8_out[7:0] = nor_2_out ? out_36[7:0] : 8'bz;  // Controlled_Buffer controlled_buffer_13
  assign controlled_buffer_8_out[15:8] = DATA_TO_MAR_HI ? out_31 : 8'bz;  // Controlled_Buffer controlled_buffer_14
  not not_3 (not_3_out, DATA_TO_MDR);
  and and_3 (CLK, or_1_out, not_2_out);
  not not_4 (minus_CLK, CLK);
  assign out_31 = IP_HI_TO_DATA ? out_33[15:8] : 8'bz;  // Controlled_Buffer controlled_buffer_15
  nor nor_3 (nor_3_out, DATA_TO_IP_HI, ADDR_TO_IP);
  or or_2 (or_2_out, DATA_TO_IP_HI, DATA_TO_IP_LO, ADDR_TO_IP);
  nor nor_4 (nor_4_out, DATA_TO_MAR_HI, ADDR_TO_MAR);
  or or_3 (or_3_out, DATA_TO_MAR_HI, DATA_TO_MAR_LO, ADDR_TO_MAR);
  assign controlled_buffer_12_out = nor_3_out ? out_33[15:8] : 8'bz;  // Controlled_Buffer controlled_buffer_16
  assign controlled_buffer_8_out[15:8] = nor_4_out ? out_36[15:8] : 8'bz;  // Controlled_Buffer controlled_buffer_17
  Counter #(.width(16), .max('hffff)) counter_1 (
    .load(or_2_out), .D({controlled_buffer_12_out, controlled_buffer_7_out}), .count(IP_INC), .Q(out_33),
    .clk(CLK), .clr(RST));  // open: carry
  Counter #(.width(16), .max('hffff)) counter_2 (
    .load(or_3_out), .D(controlled_buffer_8_out), .count(MAR_INC), .Q(out_36), .clk(CLK));  // open: carry, clr
  RAM #(.addrWidth(16)) ram_1 (.addr(out_36), .data(out_38), .sel(1'b1), .clk(CLK), .ld(not_3_out));  // open: clr
  assign out_32 = in_6 ? in_4 : 16'bz;  // Controlled_Buffer controlled_buffer_18
  assign out_32 = IP_TO_ADDR ? out_33 : 16'bz;  // Controlled_Buffer controlled_buffer_19
  assign {controlled_buffer_12_out, controlled_buffer_7_out} = ADDR_TO_IP ? out_32 : 16'bz;  // Controlled_Buffer controlled_buffer_20
  assign controlled_buffer_8_out = ADDR_TO_MAR ? out_32 : 16'bz;  // Controlled_Buffer controlled_buffer_21

  // Notes on the sheet:
  //   A Register
  //   X Register
  //   Y Register
  //   B Register
  //   C Register
  //   D Register
  //   8-Bit Data Bus
  //   Clock
  //   Instruction Pointer
  //   Memory Address Register
  //   Memory Data Register
  //   16-Bit Address Bus
endmodule
